// Logisim project DDK Lab 1 Zadacha 5.circ as structural Verilog: 1 circuit, main circuit main
module main (
  input  x,
  input  y,
  input  z,
  output f
);

  wire and_1_out, and_2_out, and_3_out, and_4_out, and_5_out, and_6_out, and_7_out, and_8_out, nor_1_out,
       not_1_out, not_2_out, not_3_out, not_4_out, not_5_out, not_6_out, not_7_out, not_8_out, or_1_out,
       or_2_out, or_3_out, or_4_out, or_5_out;

  not not_1 (not_1_out, z);
  or or_1 (or_1_out, z, x);
  and and_1 (and_1_out, not_1_out, or_1_out);
  not not_2 (not_2_out, y);
  or or_2 (or_2_out, y, and_1_out);
  and and_2 (and_2_out, not_2_out, or_2_out);
  not not_3 (not_3_out, x);
  not not_4 (not_4_out, x);
  not not_5 (not_5_out, z);
  not not_6 (not_6_out, z);
  not not_7 (not_7_out, z);
  not not_8 (not_8_out, x);
  or or_3 (or_3_out, x, and_2_out);
  or or_4 (or_4_out, x, z);
  or or_5 (or_5_out, not_3_out, y);
  and and_3 (and_3_out, x, y);
  and and_4 (and_4_out, not_4_out, not_5_out);
  and and_5 (and_5_out, y, not_6_out);
  and and_6 (and_6_out, y, not_7_out);
  and and_7 (and_7_out, not_8_out, or_3_out);
  and and_8 (and_8_out, or_4_out, or_5_out);
  nor nor_1 (nor_1_out, and_3_out, and_4_out, and_5_out);
  or or_6 (f, and_6_out, and_7_out, and_8_out, nor_1_out);
endmodule
