// Logisim project DDK Lab 1 Zadacha 7.circ as structural Verilog: 1 circuit, main circuit main
module main (
  input  x,
  input  y,
  input  z,
  output out_4
);

  or or_1 (out_4, x, y, z);
endmodule
