// Logisim project DDK Lab 1 Zadacha 9.circ as structural Verilog: 1 circuit, main circuit main
module main (
  input  in_1,
  input  y,
  input  z,
  output f
);

  wire nand_1_out, nand_2_out, nand_3_out, nand_4_out, nand_5_out;

  nand nand_1 (nand_1_out, in_1, in_1);
  nand nand_2 (nand_2_out, y, y);
  nand nand_3 (nand_3_out, nand_1_out, nand_2_out);
  nand nand_4 (nand_4_out, nand_3_out, nand_3_out);
  nand nand_5 (nand_5_out, z, z);
  nand nand_6 (f, nand_4_out, nand_5_out);
endmodule
