// Logisim project ddk lab 2 final.circ as structural Verilog: 1 circuit, main circuit main
module main (
  input  in_1,
  input  in_2,
  input  in_3,
  input  in_4,
  input  in_5
);

  wire a_out, b_out, c_out, d_out, decoder_1_out0, decoder_1_out1, decoder_1_out2, decoder_1_out3,
       decoder_1_out4, decoder_1_out5, decoder_1_out6, decoder_1_out7, decoder_1_out9, decoder_1_out10,
       decoder_1_out11, decoder_1_out12, decoder_1_out13, decoder_1_out14, decoder_1_out15, e_out, f_out,
       g_out;

  Decoder #(.select(4), .enable("false")) decoder_1 (
    .out0(decoder_1_out0), .out1(decoder_1_out1), .out2(decoder_1_out2), .out3(decoder_1_out3),
    .out4(decoder_1_out4), .out5(decoder_1_out5), .out6(decoder_1_out6), .out7(decoder_1_out7),
    .out9(decoder_1_out9), .out10(decoder_1_out10), .out11(decoder_1_out11), .out12(decoder_1_out12),
    .out13(decoder_1_out13), .out14(decoder_1_out14), .out15(decoder_1_out15), .sel({in_1, in_2, in_3, in_4}));  // open: out8
  or a (a_out, decoder_1_out1, decoder_1_out4, decoder_1_out11, decoder_1_out13);
  or b (b_out, decoder_1_out5, decoder_1_out6, decoder_1_out11, decoder_1_out12, decoder_1_out14, decoder_1_out15);
  or c (c_out, decoder_1_out2, decoder_1_out12, decoder_1_out14, decoder_1_out15);
  or d (d_out, decoder_1_out1, decoder_1_out4, decoder_1_out7, decoder_1_out10, decoder_1_out15);
  _7_Segment_Display #(.active("false")) u_7_segment_display_1 (
    .g(g_out), .f(f_out), .a(a_out), .b(b_out), .e(e_out), .d(d_out), .c(c_out), .dp(in_5));
  or e (e_out, decoder_1_out1, decoder_1_out3, decoder_1_out4, decoder_1_out5, decoder_1_out7, decoder_1_out9);
  or g (g_out, decoder_1_out0, decoder_1_out1, decoder_1_out7, decoder_1_out12);
  or f (f_out, decoder_1_out1, decoder_1_out2, decoder_1_out3, decoder_1_out7, decoder_1_out13);

  // Notes on the sheet:
  //   a={1,4,11,13}
  //   b={5,6,11,12,14,15}
  //   c={2,12,14,15}
  //   d={1,4,7,10,15}
  //   e={1,3,4,5,7,10}
  //   f={1,2,3,7,13}
  //   g={0,1,7,12}
endmodule
