// Logisim project ddk lab 2 posledna zadacha.circ as structural Verilog: 1 circuit, main circuit main
module main (
  input  [3:0] in_1,
  output out_2,
  output out_3
);

  wire decoder_1_out1, decoder_1_out3, decoder_1_out4, decoder_1_out5, decoder_1_out7, decoder_1_out9,
       decoder_1_out10, decoder_1_out15;

  Decoder #(.select(4), .enable("false")) decoder_1 (
    .out1(decoder_1_out1), .out3(decoder_1_out3), .out4(decoder_1_out4), .out5(decoder_1_out5),
    .out7(decoder_1_out7), .out9(decoder_1_out9), .out10(decoder_1_out10), .out15(decoder_1_out15), .sel(in_1));  // open: out0, out2, out6, out8, out11, out12, out13, out14
  or d (out_2, decoder_1_out1, decoder_1_out4, decoder_1_out7, decoder_1_out10, decoder_1_out15);
  or e (out_3, decoder_1_out1, decoder_1_out3, decoder_1_out4, decoder_1_out5, decoder_1_out7, decoder_1_out9);

  // Notes on the sheet:
  //   d={1,4,7,10,15}
  //   e={1,3,4,5,7,10}
endmodule
