// Logisim project ddk lab 2 zadacha 4.circ as structural Verilog: 1 circuit, main circuit main
module main (
  input  [3:0] in_1,
  input  in_2,
  output \занемарливо 
);

  wire [7:1] rom_1_data;

  ROM #(.addrWidth(4)) rom_1 (.addr(in_1), .data({rom_1_data, \занемарливо }));  // open: sel
  _7_Segment_Display #(.active("false")) u_7_segment_display_1 (
    .g(rom_1_data[1]), .f(rom_1_data[2]), .a(rom_1_data[7]), .b(rom_1_data[6]), .e(rom_1_data[3]),
    .d(rom_1_data[4]), .c(rom_1_data[5]), .dp(in_2));

  // Notes on the sheet:
  //   contents of rom_1 (hex, n*v repeats v):
  //   2 9e 24 c 98 48 40 1e 0 8 10 c0 62 84 60 70
endmodule
