// Logisim project ddk lab 2 zadacha 5 g.circ as structural Verilog: 1 circuit, main circuit main
module main (
  input  in_1,
  input  in_2,
  input  in_3,
  input  in_4,
  input  in_5,
  input  in_6,
  input  in_7,
  input  in_8,
  input  in_9,
  input  in_10,
  input  in_11,
  input  in_12,
  input  in_13,
  input  in_14,
  input  in_15,
  input  in_16,
  input  [1:0] in_17,
  input  [1:0] in_18,
  output out_19
);

  wire multiplexer_1_out, multiplexer_2_out, multiplexer_3_out, multiplexer_4_out;

  Multiplexer #(.select(2), .enable("false")) multiplexer_1 (
    .in0(in_1), .in1(in_2), .in2(in_3), .in3(in_4), .out(multiplexer_1_out), .sel(in_17));
  Multiplexer #(.select(2), .enable("false")) multiplexer_2 (
    .in0(in_5), .in1(in_6), .in2(in_7), .in3(in_8), .out(multiplexer_2_out), .sel(in_17));
  Multiplexer #(.select(2), .enable("false")) multiplexer_3 (
    .in0(in_9), .in1(in_10), .in2(in_11), .in3(in_12), .out(multiplexer_3_out), .sel(in_17));
  Multiplexer #(.select(2), .enable("false")) multiplexer_4 (
    .in0(in_13), .in1(in_14), .in2(in_15), .in3(in_16), .out(multiplexer_4_out), .sel(in_17));
  Multiplexer #(.select(2), .enable("false")) multiplexer_5 (
    .in0(multiplexer_1_out), .in1(multiplexer_2_out), .in2(multiplexer_3_out), .in3(multiplexer_4_out),
    .out(out_19), .sel(in_18));
endmodule
