// Logisim project D flip flop.circ as structural Verilog: 1 circuit, main circuit main
module main (
);

  D_Flip_Flop d_ff_1 ();  // open: clk, D, Q, Qn, preset, en, reset

  // Notes on the sheet:
  //   D - пин за внесување на вредност за D
  //   Q- Излезна вредност од флип-флопот
  //   Preset - Доделув вредност 1 на флип-флопот, асинхроно
  //   Reset - Доделува вредност 0 на флип-флопот, асинхроно
  //   Q'- Комплементирана излезна  вредност од флип-флопот
  //   Clock - Електричен сигнал што осцилира помеѓу 0 (LOW) и 1 (HIGH) за дадена фреквенција (Hz)
  //   INPUT
  //   OUTPUT
  //   INPUT
  //   Enable - Овозможува вклучување или исклучување на компонентата, дозволува проток на вредности преку клок
  //   INPUT
  //   OUTPUT
  //   Clock
  //   D
  //   Preset
  //   Q
  //   Q'
  //   Enable
  //   Reset
  //   INPUT
  //   INPUT
endmodule
