// Logisim project asinhron d latch.circ as structural Verilog: 1 circuit, main circuit main
module main (
  input  in_1,
  input  in_2,
  output out_3,
  output out_4
);

  wire clock_1_out, nand_1_out, nand_2_out, nand_3_out, nand_4_out;

  Clock clock_1 (.out(clock_1_out));
  nand nand_1 (nand_1_out, nand_4_out, nand_2_out);
  nand nand_2 (nand_2_out, nand_1_out, clock_1_out, in_2);
  nand nand_3 (nand_3_out, nand_2_out, clock_1_out, nand_4_out);
  nand nand_4 (nand_4_out, nand_3_out, in_1, in_2);
  nand nand_5 (out_3, nand_2_out, out_4);
  nand nand_6 (out_4, out_3, nand_3_out, in_2);
endmodule
