// Logisim project realizacija.circ as structural Verilog: 1 circuit, main circuit main
module main (
  input  in_1,
  input  in_2,
  output out_3
);

  wire clock_1_out, xor_1_out;

  xor xor_1 (xor_1_out, in_1, in_2);
  Clock clock_1 (.out(clock_1_out));
  J_K_Flip_Flop j_k_ff_1 (.J(xor_1_out), .clk(clock_1_out), .K(in_1), .Q(out_3));  // open: Qn, preset, en, reset
endmodule
