// Logisim project lab4 realizacija.circ as structural Verilog: 1 circuit, main circuit main
module main (
  input  x,
  output out_2
);

  wire and_1_out, and_2_out, and_3_out, and_4_out, and_5_out, and_6_out, and_7_out, clock_1_out, not_1_out,
       or_1_out, or_2_out, or_3_out, t_ff_1_q, t_ff_1_qn, t_ff_2_q, t_ff_2_qn, t_ff_3_q;

  and and_1 (and_1_out, t_ff_3_q, x);
  and and_2 (and_2_out, t_ff_1_qn, t_ff_2_qn, not_1_out);
  not not_1 (not_1_out, x);
  and and_3 (and_3_out, t_ff_2_q, x);
  and and_4 (and_4_out, not_1_out, t_ff_3_q);
  and and_5 (and_5_out, t_ff_2_q, t_ff_3_q);
  and and_6 (and_6_out, x, t_ff_1_q);
  and and_7 (and_7_out, x, t_ff_3_q, t_ff_2_q);
  or or_1 (or_1_out, t_ff_1_q, and_3_out, and_1_out, and_2_out);
  or or_2 (or_2_out, t_ff_1_q, and_7_out);
  or or_3 (or_3_out, and_4_out, and_5_out, and_6_out);
  Clock clock_1 (.out(clock_1_out));
  T_Flip_Flop t_ff_1 (.clk(clock_1_out), .T(or_2_out), .Q(t_ff_1_q), .Qn(t_ff_1_qn));  // open: preset, reset, en
  T_Flip_Flop t_ff_2 (.clk(clock_1_out), .T(or_3_out), .Q(t_ff_2_q), .Qn(t_ff_2_qn));  // open: preset, reset, en
  T_Flip_Flop t_ff_3 (.clk(clock_1_out), .T(or_1_out), .Q(t_ff_3_q));  // open: Qn, preset, reset, en
  and and_8 (out_2, t_ff_2_q, not_1_out, t_ff_3_q);
endmodule
