// Logisim project lab4.circ as structural Verilog: 1 circuit, main circuit main
module main (
  input  d,
  input  n,
  output r
);

  wire and_1_out, and_2_out, and_3_out, and_4_out, and_5_out, and_6_out, d_ff_1_q, d_ff_1_qn, d_ff_2_q,
       d_ff_2_qn, not_1_out, or_1_out, or_2_out;

  not not_1 (not_1_out, n);
  and and_1 (and_1_out, d_ff_1_q, d_ff_2_qn);
  and and_2 (and_2_out, d, d_ff_1_qn);
  and and_3 (and_3_out, n, d_ff_1_qn, d_ff_2_q);
  and and_4 (and_4_out, d_ff_1_qn, d_ff_2_q, not_1_out);
  and and_5 (and_5_out, d_ff_1_q, d_ff_2_qn, d);
  and and_6 (and_6_out, n, d_ff_2_qn);
  or or_1 (or_1_out, and_1_out, and_2_out, and_3_out);
  or or_2 (or_2_out, and_4_out, and_5_out, and_6_out);
  D_Flip_Flop d_ff_1 (.D(or_1_out), .Q(d_ff_1_q), .Qn(d_ff_1_qn));  // open: clk, preset, en, reset
  D_Flip_Flop d_ff_2 (.D(or_2_out), .Q(d_ff_2_q), .Qn(d_ff_2_qn));  // open: clk, preset, en, reset
  and and_7 (r, d_ff_1_q, d_ff_2_q);
endmodule
