// Logisim project lab5 246.circ as structural Verilog: 1 circuit, main circuit main
module main (
  input  in_1
);

  wire and_1_out, clock_1_out, d_ff_1_qn, d_ff_2_qn, d_ff_3_qn, d_ff_4_qn, d_ff_5_qn, d_ff_6_qn, d_ff_7_qn,
       d_ff_8_qn, or_1_out;
  wire [3:0] d_ff_1_q, d_ff_5_q;

  Clock clock_1 (.out(clock_1_out));
  D_Flip_Flop d_ff_1 (
    .clk(clock_1_out), .D(d_ff_1_qn), .Q(d_ff_1_q[0]), .Qn(d_ff_1_qn), .reset(or_1_out));  // open: preset, en
  D_Flip_Flop d_ff_2 (
    .clk(d_ff_1_qn), .D(d_ff_2_qn), .Q(d_ff_1_q[1]), .Qn(d_ff_2_qn), .reset(or_1_out));  // open: preset, en
  D_Flip_Flop d_ff_3 (
    .clk(d_ff_2_qn), .D(d_ff_3_qn), .Q(d_ff_1_q[2]), .Qn(d_ff_3_qn), .reset(or_1_out));  // open: preset, en
  Hex_Digit_Display hex_digit_display_1 (.value(d_ff_5_q));  // open: dp
  D_Flip_Flop d_ff_4 (
    .clk(d_ff_3_qn), .D(d_ff_4_qn), .Q(d_ff_1_q[3]), .Qn(d_ff_4_qn), .reset(or_1_out));  // open: preset, en
  Hex_Digit_Display hex_digit_display_2 (.value(d_ff_1_q));  // open: dp
  D_Flip_Flop d_ff_5 (
    .clk(d_ff_4_qn), .D(d_ff_5_qn), .Q(d_ff_5_q[0]), .Qn(d_ff_5_qn), .reset(or_1_out));  // open: preset, en
  or or_1 (or_1_out, in_1, and_1_out);
  D_Flip_Flop d_ff_6 (
    .clk(d_ff_5_qn), .D(d_ff_6_qn), .Q(d_ff_5_q[1]), .Qn(d_ff_6_qn), .reset(or_1_out));  // open: preset, en
  D_Flip_Flop d_ff_7 (
    .clk(d_ff_6_qn), .D(d_ff_7_qn), .Q(d_ff_5_q[2]), .Qn(d_ff_7_qn), .reset(or_1_out));  // open: preset, en
  D_Flip_Flop d_ff_8 (
    .clk(d_ff_7_qn), .D(d_ff_8_qn), .Q(d_ff_5_q[3]), .Qn(d_ff_8_qn), .reset(or_1_out));  // open: preset, en
  and and_1 (and_1_out, d_ff_5_q[3], d_ff_5_q[2], d_ff_5_q[1], d_ff_5_q[0], d_ff_1_q[2], d_ff_1_q[1]);
endmodule
