// Logisim project lab5 asinhron bcd.circ as structural Verilog: 1 circuit, main circuit main
// 1
module main (
);

  wire and_1_out, and_2_out, clock_1_out, d_ff_2_qn, d_ff_3_qn, d_ff_4_qn, d_ff_5_qn, or_1_out;
  wire [0:0] d_ff_1_q;
  wire [3:0] d_ff_2_q;

  Clock clock_1 (.out(clock_1_out));
  D_Flip_Flop d_ff_1 (.clk(d_ff_5_qn), .D(or_1_out), .Q(d_ff_1_q[0]), .reset(and_1_out));  // open: Qn, preset, en
  Hex_Digit_Display hex_digit_display_1 (.value({3'b000, d_ff_1_q[0]}));  // open: dp
  D_Flip_Flop d_ff_2 (
    .clk(clock_1_out), .D(d_ff_2_qn), .Q(d_ff_2_q[0]), .Qn(d_ff_2_qn), .reset(or_1_out));  // open: preset, en
  Hex_Digit_Display hex_digit_display_2 (.value(d_ff_2_q));  // open: dp
  D_Flip_Flop d_ff_3 (
    .clk(d_ff_2_qn), .D(d_ff_3_qn), .Q(d_ff_2_q[1]), .Qn(d_ff_3_qn), .reset(or_1_out));  // open: preset, en
  or or_1 (or_1_out, and_2_out, and_1_out);
  and and_1 (and_1_out, d_ff_1_q[0], d_ff_2_q[0], d_ff_2_q[2], clock_1_out);
  D_Flip_Flop d_ff_4 (
    .clk(d_ff_3_qn), .D(d_ff_4_qn), .Q(d_ff_2_q[2]), .Qn(d_ff_4_qn), .reset(or_1_out));  // open: preset, en
  D_Flip_Flop d_ff_5 (
    .clk(d_ff_4_qn), .D(d_ff_5_qn), .Q(d_ff_2_q[3]), .Qn(d_ff_5_qn), .reset(or_1_out));  // open: preset, en
  and and_2 (and_2_out, d_ff_2_q[1], d_ff_2_q[3]);
endmodule
