// Logisim project lab5 asinhron brojach modul 16.circ as structural Verilog: 1 circuit, main circuit main
module main (
  input  in_1
);

  wire clock_1_out, d_ff_1_qn, d_ff_2_qn, d_ff_3_qn, d_ff_4_qn;
  wire [3:0] d_ff_1_q;

  Clock clock_1 (.out(clock_1_out));
  D_Flip_Flop d_ff_1 (
    .clk(clock_1_out), .D(d_ff_1_qn), .Q(d_ff_1_q[0]), .Qn(d_ff_1_qn), .reset(in_1));  // open: preset, en
  Hex_Digit_Display hex_digit_display_1 (.value(d_ff_1_q));  // open: dp
  D_Flip_Flop d_ff_2 (
    .clk(d_ff_1_qn), .D(d_ff_2_qn), .Q(d_ff_1_q[1]), .Qn(d_ff_2_qn), .reset(in_1));  // open: preset, en
  D_Flip_Flop d_ff_3 (
    .clk(d_ff_2_qn), .D(d_ff_3_qn), .Q(d_ff_1_q[2]), .Qn(d_ff_3_qn), .reset(in_1));  // open: preset, en
  D_Flip_Flop d_ff_4 (
    .clk(d_ff_3_qn), .D(d_ff_4_qn), .Q(d_ff_1_q[3]), .Qn(d_ff_4_qn), .reset(in_1));  // open: preset, en
endmodule
