// Logisim project lab5 bcd 246.circ as structural Verilog: 1 circuit, main circuit main
module main (
  input  in_1
);

  wire and_1_out, and_2_out, and_3_out, clock_1_out, d_ff_1_qn, d_ff_2_qn, d_ff_3_qn, d_ff_4_qn, d_ff_5_qn,
       d_ff_6_qn, d_ff_7_qn, d_ff_8_qn, d_ff_9_qn, d_ff_10_qn, or_1_out, or_2_out, or_3_out;
  wire [1:0] d_ff_3_q;
  wire [3:0] d_ff_1_q, d_ff_2_q;

  Clock clock_1 (.out(clock_1_out));
  and and_1 (and_1_out, d_ff_1_q[2], d_ff_1_q[1], d_ff_2_q[2], d_ff_3_q[1]);
  D_Flip_Flop d_ff_1 (
    .clk(clock_1_out), .D(d_ff_1_qn), .Q(d_ff_1_q[0]), .Qn(d_ff_1_qn), .reset(or_2_out));  // open: preset, en
  D_Flip_Flop d_ff_2 (
    .clk(and_2_out), .D(d_ff_2_qn), .Q(d_ff_2_q[0]), .Qn(d_ff_2_qn), .reset(or_3_out));  // open: preset, en
  D_Flip_Flop d_ff_3 (
    .clk(and_3_out), .D(d_ff_3_qn), .Q(d_ff_3_q[0]), .Qn(d_ff_3_qn), .reset(or_1_out));  // open: preset, en
  Hex_Digit_Display hex_digit_display_1 (.value(d_ff_2_q));  // open: dp
  Hex_Digit_Display hex_digit_display_2 (.value({2'b00, d_ff_3_q}));  // open: dp
  or or_1 (or_1_out, and_1_out, in_1, and_1_out);
  Hex_Digit_Display hex_digit_display_3 (.value(d_ff_1_q));  // open: dp
  D_Flip_Flop d_ff_4 (
    .clk(d_ff_1_qn), .D(d_ff_4_qn), .Q(d_ff_1_q[1]), .Qn(d_ff_4_qn), .reset(or_2_out));  // open: preset, en
  or or_2 (or_2_out, or_3_out, in_1, and_2_out);
  D_Flip_Flop d_ff_5 (
    .clk(d_ff_2_qn), .D(d_ff_5_qn), .Q(d_ff_2_q[1]), .Qn(d_ff_5_qn), .reset(or_3_out));  // open: preset, en
  or or_3 (or_3_out, and_1_out, in_1, and_3_out);
  D_Flip_Flop d_ff_6 (
    .clk(d_ff_3_qn), .D(d_ff_6_qn), .Q(d_ff_3_q[1]), .Qn(d_ff_6_qn), .reset(or_1_out));  // open: preset, en
  D_Flip_Flop d_ff_7 (
    .clk(d_ff_4_qn), .D(d_ff_7_qn), .Q(d_ff_1_q[2]), .Qn(d_ff_7_qn), .reset(or_2_out));  // open: preset, en
  D_Flip_Flop d_ff_8 (
    .clk(d_ff_5_qn), .D(d_ff_8_qn), .Q(d_ff_2_q[2]), .Qn(d_ff_8_qn), .reset(or_3_out));  // open: preset, en
  D_Flip_Flop d_ff_9 (
    .clk(d_ff_7_qn), .D(d_ff_9_qn), .Q(d_ff_1_q[3]), .Qn(d_ff_9_qn), .reset(or_2_out));  // open: preset, en
  and and_2 (and_2_out, d_ff_1_q[3], d_ff_1_q[1]);
  D_Flip_Flop d_ff_10 (
    .clk(d_ff_8_qn), .D(d_ff_10_qn), .Q(d_ff_2_q[3]), .Qn(d_ff_10_qn), .reset(or_3_out));  // open: preset, en
  and and_3 (and_3_out, d_ff_2_q[3], d_ff_2_q[1]);
endmodule
