// Logisim project lab5 realizacija.circ as structural Verilog: 1 circuit, main circuit main
module main (
  input  in_1,
  input  in_2,
  input  in_3,
  input  in_4,
  input  in_5,
  input  [1:0] in_6,
  input  in_7
);

  wire clock_1_out, multiplexer_1_out, multiplexer_2_out, multiplexer_3_out, multiplexer_4_out;
  wire [3:0] d_ff_1_q;

  Clock clock_1 (.out(clock_1_out));
  Multiplexer #(.select(2), .enable("false")) multiplexer_1 (
    .in0(in_1), .in1(d_ff_1_q[1]), .in2(in_5), .in3(d_ff_1_q[0]), .out(multiplexer_1_out), .sel(in_6));
  Hex_Digit_Display hex_digit_display_1 (.value(d_ff_1_q));  // open: dp
  D_Flip_Flop d_ff_1 (.clk(clock_1_out), .D(multiplexer_1_out), .Q(d_ff_1_q[0]), .reset(in_7));  // open: Qn, preset, en
  Multiplexer #(.select(2), .enable("false")) multiplexer_2 (
    .in0(in_2), .in1(d_ff_1_q[2]), .in2(d_ff_1_q[0]), .in3(d_ff_1_q[1]), .out(multiplexer_2_out), .sel(in_6));
  D_Flip_Flop d_ff_2 (.clk(clock_1_out), .D(multiplexer_2_out), .Q(d_ff_1_q[1]), .reset(in_7));  // open: Qn, preset, en
  Multiplexer #(.select(2), .enable("false")) multiplexer_3 (
    .in0(in_3), .in1(d_ff_1_q[3]), .in2(d_ff_1_q[1]), .in3(d_ff_1_q[2]), .out(multiplexer_3_out), .sel(in_6));
  D_Flip_Flop d_ff_3 (.clk(clock_1_out), .D(multiplexer_3_out), .Q(d_ff_1_q[2]), .reset(in_7));  // open: Qn, preset, en
  Multiplexer #(.select(2), .enable("false")) multiplexer_4 (
    .in0(in_4), .in1(d_ff_1_q[0]), .in2(d_ff_1_q[2]), .in3(d_ff_1_q[3]), .out(multiplexer_4_out), .sel(in_6));
  D_Flip_Flop d_ff_4 (.clk(clock_1_out), .D(multiplexer_4_out), .Q(d_ff_1_q[3]), .reset(in_7));  // open: Qn, preset, en
endmodule
